# Fritzing sketch keypad - Calculator (saved by Fritzing 0.9.4)

parts:
  Part1 = Arduino Uno (Rev3)
  Part2 = 4x4 Keypad [part_number=101207]

nets:
  N1: Part1.D8, Part2.7
  N2: Part1.D9_PWM, Part2.8
  N3: Part1.D2, Part2.1
  N4: Part1.D3_PWM, Part2.2
  N5: Part1.D4, Part2.3
  N6: Part1.D5_PWM, Part2.4
  N7: Part1.D6_PWM, Part2.5
  N8: Part1.D7, Part2.6

custom parts:
  4x4 Keypad: Matrix membrane keypad 4x4
